// Logisim project add.circ as structural Verilog: 2 circuits, main circuit main
module main (
  input  a,
  input  b,
  output sum,
  output count
);

  xor xor_1 (sum, a, b);
  and and_1 (count, a, b);
endmodule

module exercise (
  input  in_1,
  input  in_2,
  output out_3,
  output out_4
);

  main main_1 (.a(in_1), .b(in_2), .sum(out_3), .count(out_4));
endmodule
