// Logisim project 实验1.1.circ as structural Verilog: 1 circuit, main circuit main
module main (
);

  DotMatrix #(.matrixcols(14), .matrixrows(16)) dotmatrix_1 (
    .col0({16{1'b0}}), .col1({16{1'b0}}), .col2(16'h1088), .col3(16'h1108), .col4(16'h1288), .col5(16'h1488),
    .col6(16'h1889), .col7(16'hff8f), .col8(16'h1898), .col9(16'h14a8), .col10(16'h12c8), .col11(16'h1108),
    .col12(16'h1088), .col13({16{1'b0}}));
  DotMatrix #(.matrixcols(14), .matrixrows(16)) dotmatrix_2 (
    .col0({16{1'b0}}), .col1(16'h1), .col2(16'h7f11), .col3(16'h4911), .col4(16'h491d), .col5(16'h4917),
    .col6(16'h49d1), .col7(16'h4971), .col8(16'h4917), .col9(16'h491d), .col10(16'h4911), .col11(16'h7f11),
    .col12(16'h1), .col13({16{1'b0}}));
  DotMatrix #(.matrixcols(14), .matrixrows(16)) dotmatrix_3 (
    .col0({16{1'b0}}), .col1(16'h1040), .col2(16'h1080), .col3(16'h5100), .col4(16'h33ff), .col5(16'h1500),
    .col6(16'h1880), .col7({16{1'b0}}), .col8({16{1'b0}}), .col9(16'h3fff), .col10(16'h2110),
    .col11(16'h2310), .col12(16'h2520), .col13(16'h38c0));
endmodule
