// Logisim project 实验1.3.circ as structural Verilog: 9 circuits, main circuit main
module main (
  input  in_1,
  input  in_2,
  input  in_3,
  input  in_4,
  input  in_5,
  output out_6,
  output out_7,
  output out_8
);

  wire transistor_2_out, transistor_9_out;

  Transistor transistor_1 (.in(1'b0), .out(out_7), .gate(in_3));
  Transistor #(.\type ("n")) transistor_2 (.in(1'b1), .out(transistor_2_out), .gate(in_1));
  Transistor #(.\type ("n")) transistor_3 (.in(transistor_2_out), .out(out_7), .gate(in_3));
  Transistor transistor_4 (.in(1'b0), .out(out_7), .gate(in_1));
  Transistor transistor_5 (.in(1'b1), .out(out_8), .gate(in_5));
  Transistor #(.\type ("n")) transistor_6 (.in(1'b0), .out(out_8), .gate(in_5));
  Transistor #(.\type ("n")) transistor_7 (.in(1'b1), .out(out_6), .gate(in_2));
  Transistor transistor_8 (.in(transistor_9_out), .out(out_6), .gate(in_4));
  Transistor transistor_9 (.in(1'b0), .out(transistor_9_out), .gate(in_2));
  Transistor #(.\type ("n")) transistor_10 (.in(1'b1), .out(out_6), .gate(in_4));
endmodule

module \与门  (
  input  in_1,
  input  in_2,
  output out_3
);

  wire transistor_2_out;

  Transistor transistor_1 (.in(1'b0), .out(out_3), .gate(in_2));
  Transistor #(.\type ("n")) transistor_2 (.in(1'b1), .out(transistor_2_out), .gate(in_1));
  Transistor #(.\type ("n")) transistor_3 (.in(transistor_2_out), .out(out_3), .gate(in_2));
  Transistor transistor_4 (.in(1'b0), .out(out_3), .gate(in_1));

  // Notes on the sheet:
  //   与门
  //   李昱祁_PB18071496
endmodule

module \或门  (
  input  in_1,
  input  in_2,
  output out_3
);

  wire transistor_4_out;

  Transistor #(.\type ("n")) transistor_1 (.in(1'b1), .out(out_3), .gate(in_1));
  Transistor #(.\type ("n")) transistor_2 (.in(1'b1), .out(out_3), .gate(in_2));
  Transistor transistor_3 (.in(transistor_4_out), .out(out_3), .gate(in_2));
  Transistor transistor_4 (.in(1'b0), .out(transistor_4_out), .gate(in_1));

  // Notes on the sheet:
  //   或门
  //   李昱祁_PB18071496
endmodule

module \非门  (
  input  in_1,
  output out_2
);

  Transistor transistor_1 (.in(1'b1), .out(out_2), .gate(in_1));
  Transistor #(.\type ("n")) transistor_2 (.in(1'b0), .out(out_2), .gate(in_1));

  // Notes on the sheet:
  //   非门
  //   李昱祁_PB18071496
endmodule

module \实验1_4  (
  input  S,
  input  A,
  input  B,
  output D
);

  wire \与门_1_out_3 , \与门_2_out_3 , \非门_1_out_2 ;

  \非门  \u_非门_1  (.in_1(S), .out_2(\非门_1_out_2 ));
  \与门  \u_与门_1  (.in_1(\非门_1_out_2 ), .in_2(A), .out_3(\与门_1_out_3 ));
  \与门  \u_与门_2  (.in_1(S), .in_2(B), .out_3(\与门_2_out_3 ));
  \或门  \u_或门_1  (.in_1(\与门_1_out_3 ), .in_2(\与门_2_out_3 ), .out_3(D));

  // Notes on the sheet:
  //   输入A和B
  //   1-bit宽数据选择器
  //   根据S选择输出D
endmodule

module \与非门  (
  input  in_1,
  input  in_2,
  output out_3
);

  wire transistor_3_out;

  Transistor transistor_1 (.in(1'b1), .out(out_3), .gate(in_1));
  Transistor #(.\type ("n")) transistor_2 (.in(transistor_3_out), .out(out_3), .gate(in_1));
  Transistor #(.\type ("n")) transistor_3 (.in(1'b0), .out(transistor_3_out), .gate(in_2));
  Transistor transistor_4 (.in(1'b1), .out(out_3), .gate(in_2));

  // Notes on the sheet:
  //   PB18071496_李昱祁
  //   与非门
endmodule

module \或非门  (
  input  in_1,
  input  in_2,
  output out_3
);

  wire transistor_2_out;

  Transistor #(.\type ("n")) transistor_1 (.in(1'b0), .out(out_3), .gate(in_2));
  Transistor transistor_2 (.in(1'b1), .out(transistor_2_out), .gate(in_1));
  Transistor transistor_3 (.in(transistor_2_out), .out(out_3), .gate(in_2));
  Transistor #(.\type ("n")) transistor_4 (.in(1'b0), .out(out_3), .gate(in_1));

  // Notes on the sheet:
  //   PB18071496_李昱祁
  //   或非门
endmodule

module \_1_bit4选1  (
  input  in_1,
  input  in_2,
  input  in_3,
  input  in_4,
  input  in_5,
  input  in_6,
  output out_7
);

  wire \实验1_4_1_d , \实验1_4_2_d ;

  \实验1_4  \u_实验1_4_1  (.S(in_2), .A(in_3), .B(in_4), .D(\实验1_4_1_d ));
  \实验1_4  \u_实验1_4_2  (.S(in_2), .A(in_5), .B(in_6), .D(\实验1_4_2_d ));
  \实验1_4  \u_实验1_4_3  (.S(in_1), .A(\实验1_4_1_d ), .B(\实验1_4_2_d ), .D(out_7));
endmodule

module \_2_bit4选1  (
  input  in_1,
  input  in_2,
  input  in_3,
  input  in_4,
  input  in_5,
  input  in_6,
  input  in_7,
  input  in_8,
  input  in_9,
  input  in_10,
  output out_11,
  output out_12
);

  \_1_bit4选1  \u_1_bit4选1_1  (
    .in_1(in_1), .in_2(in_2), .in_3(in_3), .in_4(in_4), .in_5(in_5), .in_6(in_6), .out_7(out_11));
  \_1_bit4选1  \u_1_bit4选1_2  (
    .in_1(in_1), .in_2(in_2), .in_3(in_7), .in_4(in_8), .in_5(in_9), .in_6(in_10), .out_7(out_12));
endmodule
