// Logisim project 题目1.circ as structural Verilog: 3 circuits, main circuit main
module main (
  input  in_1,
  input  in_2
);
endmodule

module \生成电路  (
  input  a,
  input  b,
  input  c,
  output x,
  output y
);

  wire nand_1_out, nand_2_out, nand_3_out, nand_4_out, nand_5_out, nand_6_out, nand_7_out, nand_8_out,
       nand_9_out, nand_10_out, nand_11_out, nand_12_out, nand_13_out, nand_14_out, nand_15_out, nand_16_out,
       nand_17_out, nand_18_out, nand_19_out, nand_20_out, nand_21_out, nand_22_out, nand_23_out,
       nand_24_out, nand_25_out, nand_26_out, nand_27_out, nand_28_out, nand_29_out, nand_30_out,
       nand_31_out, nand_32_out, nand_33_out, nand_34_out, nand_35_out, nand_36_out, nand_37_out,
       nand_38_out, nand_39_out, nand_40_out, nand_41_out, nand_42_out, nand_43_out, nand_44_out,
       nand_45_out, nand_46_out, nand_47_out, nand_48_out, nand_49_out, nand_50_out, nand_51_out,
       nand_52_out, nand_53_out, nand_54_out, nand_55_out, nand_56_out, nand_57_out, nand_58_out,
       nand_59_out, nand_60_out, nand_62_out, nand_63_out, nand_64_out, nand_65_out, nand_66_out, nand_67_out;

  nand nand_1 (nand_1_out, a, a);
  nand nand_2 (nand_2_out, b, b);
  nand nand_3 (nand_3_out, a, a);
  nand nand_4 (nand_4_out, b, b);
  nand nand_5 (nand_5_out, a, a);
  nand nand_6 (nand_6_out, a, a);
  nand nand_7 (nand_7_out, a, a);
  nand nand_8 (nand_8_out, b, b);
  nand nand_9 (nand_9_out, a, a);
  nand nand_10 (nand_10_out, b, b);
  nand nand_11 (nand_11_out, a, a);
  nand nand_12 (nand_12_out, a, a);
  nand nand_13 (nand_13_out, b, b);
  nand nand_14 (nand_14_out, b, b);
  nand nand_15 (nand_15_out, b, b);
  nand nand_16 (nand_16_out, b, b);
  nand nand_17 (nand_17_out, b, c);
  nand nand_18 (nand_18_out, a, c);
  nand nand_19 (nand_19_out, b, c);
  nand nand_20 (nand_20_out, a, c);
  nand nand_21 (nand_21_out, nand_1_out, nand_2_out);
  nand nand_22 (nand_22_out, nand_3_out, nand_4_out);
  nand nand_23 (nand_23_out, nand_5_out, b);
  nand nand_24 (nand_24_out, nand_6_out, b);
  nand nand_25 (nand_25_out, nand_7_out, nand_8_out);
  nand nand_26 (nand_26_out, nand_9_out, nand_10_out);
  nand nand_27 (nand_27_out, nand_11_out, b);
  nand nand_28 (nand_28_out, nand_12_out, b);
  nand nand_29 (nand_29_out, a, nand_13_out);
  nand nand_30 (nand_30_out, a, nand_14_out);
  nand nand_31 (nand_31_out, a, b);
  nand nand_32 (nand_32_out, a, b);
  nand nand_33 (nand_33_out, a, nand_15_out);
  nand nand_34 (nand_34_out, a, nand_16_out);
  nand nand_35 (nand_35_out, a, b);
  nand nand_36 (nand_36_out, a, b);
  nand nand_37 (nand_37_out, nand_17_out, nand_18_out);
  nand nand_38 (nand_38_out, nand_19_out, nand_20_out);
  nand nand_39 (nand_39_out, nand_21_out, nand_22_out);
  nand nand_40 (nand_40_out, nand_23_out, nand_24_out);
  nand nand_41 (nand_41_out, c, c);
  nand nand_42 (nand_42_out, nand_25_out, nand_26_out);
  nand nand_43 (nand_43_out, nand_27_out, nand_28_out);
  nand nand_44 (nand_44_out, c, c);
  nand nand_45 (nand_45_out, nand_29_out, nand_30_out);
  nand nand_46 (nand_46_out, c, c);
  nand nand_47 (nand_47_out, nand_31_out, nand_32_out);
  nand nand_48 (nand_48_out, nand_33_out, nand_34_out);
  nand nand_49 (nand_49_out, c, c);
  nand nand_50 (nand_50_out, nand_35_out, nand_36_out);
  nand nand_51 (nand_51_out, nand_37_out, nand_38_out);
  nand nand_52 (nand_52_out, a, b);
  nand nand_53 (nand_53_out, nand_39_out, c);
  nand nand_54 (nand_54_out, nand_40_out, nand_41_out);
  nand nand_55 (nand_55_out, nand_42_out, c);
  nand nand_56 (nand_56_out, nand_43_out, nand_44_out);
  nand nand_57 (nand_57_out, nand_45_out, nand_46_out);
  nand nand_58 (nand_58_out, nand_47_out, c);
  nand nand_59 (nand_59_out, nand_48_out, nand_49_out);
  nand nand_60 (nand_60_out, nand_50_out, c);
  nand nand_61 (y, nand_51_out, nand_52_out);
  nand nand_62 (nand_62_out, nand_53_out, nand_54_out);
  nand nand_63 (nand_63_out, nand_55_out, nand_56_out);
  nand nand_64 (nand_64_out, nand_57_out, nand_58_out);
  nand nand_65 (nand_65_out, nand_59_out, nand_60_out);
  nand nand_66 (nand_66_out, nand_62_out, nand_63_out);
  nand nand_67 (nand_67_out, nand_64_out, nand_65_out);
  nand nand_68 (x, nand_66_out, nand_67_out);
endmodule

module \生成电路_2  (
  input  a,
  input  b,
  input  c,
  output x,
  output y
);

  wire and_1_out, and_2_out, and_3_out, and_4_out, and_5_out, and_6_out, and_7_out, not_1_out, not_2_out,
       not_3_out, not_4_out, not_5_out, not_6_out;

  not not_1 (not_1_out, a);
  not not_2 (not_2_out, b);
  not not_3 (not_3_out, a);
  not not_4 (not_4_out, c);
  not not_5 (not_5_out, b);
  not not_6 (not_6_out, c);
  and and_1 (and_1_out, b, c);
  and and_2 (and_2_out, a, c);
  and and_3 (and_3_out, a, b);
  and and_4 (and_4_out, not_1_out, not_2_out, c);
  and and_5 (and_5_out, not_3_out, b, not_4_out);
  and and_6 (and_6_out, a, not_5_out, not_6_out);
  and and_7 (and_7_out, a, b, c);
  or or_1 (y, and_1_out, and_2_out, and_3_out);
  or or_2 (x, and_4_out, and_5_out, and_6_out, and_7_out);

  // Notes on the sheet:
  //   PB18071496_李昱祁
endmodule
