// Logisim project 题目2.circ as structural Verilog
module \生成电路_by_expression  (
  input  G1,
  input  G2,
  input  G3,
  input  A2,
  input  A1,
  input  A0,
  output Y7,
  output Y6,
  output Y5,
  output Y4,
  output Y3,
  output Y2,
  output Y1,
  output Y0
);

  wire not_1_out, not_2_out, not_3_out, not_4_out, not_5_out, not_6_out, not_7_out, not_8_out, not_9_out,
       not_10_out, not_11_out, not_12_out, not_13_out, not_14_out, not_15_out, not_16_out, not_17_out,
       not_18_out, not_19_out, not_20_out;

  not not_1 (not_1_out, G1);
  not not_2 (not_2_out, A2);
  not not_3 (not_3_out, A1);
  not not_4 (not_4_out, A0);
  not not_5 (not_5_out, G1);
  not not_6 (not_6_out, A2);
  not not_7 (not_7_out, A1);
  not not_8 (not_8_out, G1);
  not not_9 (not_9_out, A2);
  not not_10 (not_10_out, A0);
  not not_11 (not_11_out, G1);
  not not_12 (not_12_out, A2);
  not not_13 (not_13_out, G1);
  not not_14 (not_14_out, A1);
  not not_15 (not_15_out, A0);
  not not_16 (not_16_out, G1);
  not not_17 (not_17_out, A1);
  not not_18 (not_18_out, G1);
  not not_19 (not_19_out, A0);
  not not_20 (not_20_out, G1);
  or or_1 (Y7, not_1_out, not_2_out, not_3_out, not_4_out, G3, G2);
  or or_2 (Y6, not_5_out, not_6_out, not_7_out, A0, G3, G2);
  or or_3 (Y5, not_8_out, not_9_out, not_10_out, A1, G3, G2);
  or or_4 (Y4, not_11_out, not_12_out, A0, A1, G3, G2);
  or or_5 (Y3, not_13_out, not_14_out, not_15_out, A2, G3, G2);
  or or_6 (Y2, not_16_out, not_17_out, A0, A2, G3, G2);
  or or_7 (Y1, not_18_out, not_19_out, A1, A2, G3, G2);
  or or_8 (Y0, not_20_out, A0, A1, A2, G3, G2);

  // Notes on the sheet:
  //   PB18071496_李昱祁
endmodule
