// Logisim project 题目3&4.circ as structural Verilog
module \_1_bit二选一  (
  input  in_1,
  input  in_2,
  input  in_3,
  output out_4
);

  wire and_1_out, and_2_out, not_1_out;

  not not_1 (not_1_out, in_1);
  and and_1 (and_1_out, not_1_out, in_2);
  and and_2 (and_2_out, in_1, in_3);
  or or_1 (out_4, and_1_out, and_2_out);
endmodule

module \_1_bit四选一  (
  input  in_1,
  input  in_2,
  input  in_3,
  input  in_4,
  input  in_5,
  input  in_6,
  output out_7
);

  wire \n1_bit二选一_1_out_4 , \n1_bit二选一_2_out_4 ;

  \_1_bit二选一  \u_1_bit二选一_1  (.in_1(in_1), .in_2(in_3), .in_3(in_4), .out_4(\n1_bit二选一_1_out_4 ));
  \_1_bit二选一  \u_1_bit二选一_2  (.in_1(in_1), .in_2(in_5), .in_3(in_6), .out_4(\n1_bit二选一_2_out_4 ));
  \_1_bit二选一  \u_1_bit二选一_3  (.in_1(in_2), .in_2(\n1_bit二选一_1_out_4 ), .in_3(\n1_bit二选一_2_out_4 ), .out_4(out_7));

  // Notes on the sheet:
  //   PB18071496李昱祁
endmodule
