// Logisim project 实验过程.circ as structural Verilog: 20 circuits, main circuit main
module main (
  input  in_1,
  output out_2,
  output out_3
);

  not not_1 (out_2, out_3);
  not not_2 (out_3, out_2);
endmodule

module \SR锁存器__与非门搭建  (
  input  S,
  input  R,
  output Q,
  output nQ
);

  nand nand_1 (Q, S, nQ);
  nand nand_2 (nQ, Q, R);

  // Notes on the sheet:
  //   低电平有效
  //   PB18071496
  //   约束条件S+R=1
endmodule

module \同步置位D触发器  (
  input  D,
  input  ST_N,
  output Q,
  output nQ
);

  wire CLK_out, not_1_out, or_1_out;

  Clock CLK (.out(CLK_out));
  not not_1 (not_1_out, ST_N);
  or or_1 (or_1_out, D, not_1_out);
  \D触发器  \d触发器_1  (.in_2(or_1_out), .out_5(Q), .out_6(nQ), .in_1(CLK_out));  // open: in_3, in_4

  // Notes on the sheet:
  //   PB18071496
endmodule

module \异步复位D触发器  (
  input  D,
  input  RESET_N,
  output Q,
  output nQ
);

  wire A_out, B_out, C_out, clk_out, D_out;

  Clock clk (.out(clk_out));
  nand A (A_out, D_out, B_out);
  nand B (B_out, A_out, clk_out, RESET_N);
  nand C (C_out, B_out, clk_out, D_out);
  nand u_D (D_out, C_out, D);
  nand E (Q, B_out, nQ);
  nand F (nQ, Q, C_out, RESET_N);

  // Notes on the sheet:
  //   异步复位-D触发器
  //   PB18071496
endmodule

module \_4_bit计数器  (
  input  in_1,
  output [3:0] out_2
);

  wire clock_1_out;
  wire [3:0] adder_1_out;

  Adder #(.width(4)) adder_1 (.a(out_2), .b(4'b0001), .out(adder_1_out), .cin(1'b0));  // open: cout
  Clock clock_1 (.out(clock_1_out));
  \异步D触发器_搭_寄存器  \u_异步d触发器_搭_寄存器_1  (.in_1(adder_1_out), .RST_N(in_1), .out_4(out_2), .in_2(clock_1_out));

  // Notes on the sheet:
  //   PB18071496
endmodule

module \递减计数器  (
  input  RST,
  output [3:0] out_2
);

  wire and_1_out, and_2_out, and_3_out, and_4_out, CLK_out, not_1_out, not_2_out, not_3_out, or_1_out,
       or_2_out, or_3_out;
  wire [3:0] subtractor_1_out;

  Subtractor #(.width(4)) subtractor_1 (.a(out_2), .b(4'b0001), .out(subtractor_1_out), .bin(1'b0));  // open: bout
  Clock CLK (.out(CLK_out));
  not not_1 (not_1_out, RST);
  not not_2 (not_2_out, not_1_out);
  not not_3 (not_3_out, not_1_out);
  and and_1 (and_1_out, subtractor_1_out[1], or_3_out);
  or or_1 (or_1_out, not_2_out, subtractor_1_out[3]);
  and and_2 (and_2_out, not_1_out, and_4_out);
  and and_3 (and_3_out, not_1_out, and_1_out);
  or or_2 (or_2_out, not_3_out, subtractor_1_out[0]);
  and and_4 (and_4_out, subtractor_1_out[2], or_3_out);
  \D触发器  \d触发器_1  (.in_2(or_1_out), .out_5(out_2[3]), .in_1(CLK_out));  // open: out_6, in_3, in_4
  \D触发器  \d触发器_2  (.in_2(and_2_out), .out_5(out_2[2]), .in_1(CLK_out));  // open: out_6, in_3, in_4
  \D触发器  \d触发器_3  (.in_2(and_3_out), .out_5(out_2[1]), .in_1(CLK_out));  // open: out_6, in_3, in_4
  \D触发器  \d触发器_4  (.in_2(or_2_out), .out_5(out_2[0]), .in_1(CLK_out));  // open: out_6, in_3, in_4
  or or_3 (or_3_out, out_2[3], out_2[2], out_2[1], out_2[0]);

  // Notes on the sheet:
  //   PB18071496
endmodule

module \题目5_改为高电平复位  (
  input  D,
  input  RESET,
  output Q,
  output nQ
);

  wire clock_1_out, nand_1_out, nand_2_out, nand_3_out, nand_4_out, not_1_out;

  Clock clock_1 (.out(clock_1_out));
  not not_1 (not_1_out, RESET);
  nand nand_1 (nand_1_out, nand_4_out, nand_2_out);
  nand nand_2 (nand_2_out, nand_1_out, clock_1_out, not_1_out);
  nand nand_3 (nand_3_out, nand_2_out, clock_1_out, nand_4_out);
  nand nand_4 (nand_4_out, nand_3_out, D, not_1_out);
  nand nand_5 (Q, nand_2_out, nQ);
  nand nand_6 (nQ, Q, nand_3_out, not_1_out);

  // Notes on the sheet:
  //   异步复位-D触发器
endmodule

module step1 (
  output out_1,
  output out_2
);

  not not_1 (out_1, out_2);
  not not_2 (out_2, out_1);
endmodule

module \SR锁存器  (
  input  R,
  input  S,
  output Q,
  output nQ
);

  nor nor_1 (Q, R, nQ);
  nor nor_2 (nQ, Q, S);
endmodule

module \D锁存器  (
  input  CLK,
  input  D,
  output out_3,
  output out_4
);

  wire and_1_out, and_2_out, not_1_out;

  not not_1 (not_1_out, D);
  and and_1 (and_1_out, CLK, not_1_out);
  and and_2 (and_2_out, CLK, D);
  \SR锁存器  \sr锁存器_1  (.R(and_1_out), .S(and_2_out), .Q(out_3), .nQ(out_4));
endmodule

module \D触发器  (
  input  in_1,
  input  in_2,
  input  in_3,
  input  in_4,
  output out_5,
  output out_6
);

  wire \d锁存器_1_out_3 , nand_1_out, nand_2_out, not_1_out;

  not not_1 (not_1_out, in_1);
  \D锁存器  \d锁存器_1  (.CLK(not_1_out), .D(in_2), .out_3(\d锁存器_1_out_3 ));  // open: out_4
  nand nand_1 (nand_1_out, in_3, nand_2_out);
  nand nand_2 (nand_2_out, nand_1_out, in_4);
  \D锁存器  \d锁存器_2  (.CLK(in_1), .D(\d锁存器_1_out_3 ), .out_3(out_5), .out_4(out_6));
endmodule

module \D触发器_带clk信号  (
  input  D,
  output Q,
  output out_3
);

  wire clock_1_out, \d锁存器_1_out_3 , not_1_out;

  Clock clock_1 (.out(clock_1_out));
  not not_1 (not_1_out, clock_1_out);
  \D锁存器  \d锁存器_1  (.CLK(not_1_out), .D(D), .out_3(\d锁存器_1_out_3 ));  // open: out_4
  \D锁存器  \d锁存器_2  (.CLK(clock_1_out), .D(\d锁存器_1_out_3 ), .out_3(Q), .out_4(out_3));

  // Notes on the sheet:
  //   CLK
  //   /Q
endmodule

module \_4_bit寄存器  (
  input  [3:0] in_1,
  input  RST_N,
  output [3:0] out_3
);

  wire and_1_out, and_2_out, and_3_out, and_4_out, CLK_out;

  Clock CLK (.out(CLK_out));
  and and_1 (and_1_out, RST_N, in_1[3]);
  and and_2 (and_2_out, RST_N, in_1[2]);
  and and_3 (and_3_out, RST_N, in_1[1]);
  and and_4 (and_4_out, RST_N, in_1[0]);
  \D触发器  \d触发器_1  (.in_2(and_1_out), .out_5(out_3[3]), .in_1(CLK_out));  // open: out_6, in_3, in_4
  \D触发器  \d触发器_2  (.in_2(and_2_out), .out_5(out_3[2]), .in_1(CLK_out));  // open: out_6, in_3, in_4
  \D触发器  \d触发器_3  (.in_2(and_3_out), .out_5(out_3[1]), .in_1(CLK_out));  // open: out_6, in_3, in_4
  \D触发器  \d触发器_4  (.in_2(and_4_out), .out_5(out_3[0]), .in_1(CLK_out));  // open: out_6, in_3, in_4

  // Notes on the sheet:
  //   PB18071496
endmodule

module \_4_bit寄存器_封装  (
  input  [3:0] in_1,
  input  in_2,
  input  in_3,
  output [3:0] out_4
);

  wire and_1_out, and_2_out, and_3_out, and_4_out;

  and and_1 (and_1_out, in_3, in_1[3]);
  and and_2 (and_2_out, in_3, in_1[2]);
  and and_3 (and_3_out, in_3, in_1[1]);
  and and_4 (and_4_out, in_3, in_1[0]);
  \D触发器  \d触发器_1  (.in_2(and_1_out), .out_5(out_4[3]), .in_1(in_2));  // open: out_6, in_3, in_4
  \D触发器  \d触发器_2  (.in_2(and_2_out), .out_5(out_4[2]), .in_1(in_2));  // open: out_6, in_3, in_4
  \D触发器  \d触发器_3  (.in_2(and_3_out), .out_5(out_4[1]), .in_1(in_2));  // open: out_6, in_3, in_4
  \D触发器  \d触发器_4  (.in_2(and_4_out), .out_5(out_4[0]), .in_1(in_2));  // open: out_6, in_3, in_4
endmodule

module \_0_15循环计数_step6  (
  input  RST_N,
  output [3:0] out_2
);

  wire CLK_out;
  wire [3:0] adder_1_out;

  Clock CLK (.out(CLK_out));
  Adder #(.width(4)) adder_1 (.a(out_2), .b(4'b0001), .out(adder_1_out), .cin(1'b0));  // open: cout
  \_4_bit寄存器_封装  \u_4_bit寄存器_封装_1  (.in_1(adder_1_out), .in_2(CLK_out), .in_3(RST_N), .out_4(out_2));

  // Notes on the sheet:
  //   PB18071496
endmodule

module \_9_0循环递减计数器  (
  input  RST_N,
  output [3:0] out_2
);

  wire and_1_out, and_2_out, and_3_out, and_4_out, and_5_out, and_6_out, CLK_out, or_1_out;
  wire [3:0] subtractor_1_out;

  Subtractor #(.width(4)) subtractor_1 (.a(out_2), .b(4'b0001), .out(subtractor_1_out), .bin(1'b0));  // open: bout
  Clock CLK (.out(CLK_out));
  and and_1 (and_1_out, subtractor_1_out[1], or_1_out);
  and and_2 (and_2_out, RST_N, subtractor_1_out[3]);
  and and_3 (and_3_out, RST_N, and_6_out);
  and and_4 (and_4_out, RST_N, and_1_out);
  and and_5 (and_5_out, RST_N, subtractor_1_out[0]);
  and and_6 (and_6_out, subtractor_1_out[2], or_1_out);
  \D触发器  \d触发器_1  (.in_2(and_2_out), .out_5(out_2[3]), .in_1(CLK_out));  // open: out_6, in_3, in_4
  \D触发器  \d触发器_2  (.in_2(and_3_out), .out_5(out_2[2]), .in_1(CLK_out));  // open: out_6, in_3, in_4
  \D触发器  \d触发器_3  (.in_2(and_4_out), .out_5(out_2[1]), .in_1(CLK_out));  // open: out_6, in_3, in_4
  \D触发器  \d触发器_4  (.in_2(and_5_out), .out_5(out_2[0]), .in_1(CLK_out));  // open: out_6, in_3, in_4
  or or_1 (or_1_out, out_2[3], out_2[2], out_2[1], out_2[0]);
endmodule

module \异步复位D触发器_封装  (
  input  CLK,
  input  D,
  input  RESET_N,
  output Q,
  output nQ
);

  wire nand_1_out, nand_2_out, nand_3_out, nand_4_out;

  nand nand_1 (nand_1_out, nand_4_out, nand_2_out);
  nand nand_2 (nand_2_out, nand_1_out, CLK, RESET_N);
  nand nand_3 (nand_3_out, nand_2_out, CLK, nand_4_out);
  nand nand_4 (nand_4_out, nand_3_out, D, RESET_N);
  nand nand_5 (Q, nand_2_out, nQ);
  nand nand_6 (nQ, Q, nand_3_out, RESET_N);

  // Notes on the sheet:
  //   异步复位-D触发器
endmodule

module \异步D触发器_搭_寄存器  (
  input  [3:0] in_1,
  input  in_2,
  input  RST_N,
  output [3:0] out_4
);

  \异步复位D触发器_封装  \u_异步复位d触发器_封装_1  (.CLK(in_2), .D(in_1[3]), .RESET_N(RST_N), .Q(out_4[3]));  // open: nQ
  \异步复位D触发器_封装  \u_异步复位d触发器_封装_2  (.CLK(in_2), .D(in_1[2]), .RESET_N(RST_N), .Q(out_4[2]));  // open: nQ
  \异步复位D触发器_封装  \u_异步复位d触发器_封装_3  (.CLK(in_2), .D(in_1[1]), .RESET_N(RST_N), .Q(out_4[1]));  // open: nQ
  \异步复位D触发器_封装  \u_异步复位d触发器_封装_4  (.CLK(in_2), .D(in_1[0]), .RESET_N(RST_N), .Q(out_4[0]));  // open: nQ
endmodule

module TEST (
  input  D,
  output Q,
  output nQ
);

  wire A_out, B_out, C_out, clock_1_out, D_out;

  Clock clock_1 (.out(clock_1_out));
  nand A (A_out, D_out, B_out);
  nand B (B_out, A_out, clock_1_out);
  nand C (C_out, B_out, clock_1_out, D_out);
  nand u_D (D_out, C_out, D);
  nand E (Q, B_out, nQ);
  nand F (nQ, Q, C_out);
endmodule

module \异步复位D搭寄存器  (
  input  [3:0] in_1,
  input  RST_N,
  output [3:0] out_3
);

  wire clock_1_out;

  Clock clock_1 (.out(clock_1_out));
  \异步复位D触发器_封装  \u_异步复位d触发器_封装_1  (.CLK(clock_1_out), .D(in_1[3]), .RESET_N(RST_N), .Q(out_3[3]));  // open: nQ
  \异步复位D触发器_封装  \u_异步复位d触发器_封装_2  (.CLK(clock_1_out), .D(in_1[2]), .RESET_N(RST_N), .Q(out_3[2]));  // open: nQ
  \异步复位D触发器_封装  \u_异步复位d触发器_封装_3  (.CLK(clock_1_out), .D(in_1[1]), .RESET_N(RST_N), .Q(out_3[1]));  // open: nQ
  \异步复位D触发器_封装  \u_异步复位d触发器_封装_4  (.CLK(clock_1_out), .D(in_1[0]), .RESET_N(RST_N), .Q(out_3[0]));  // open: nQ
endmodule
